// Logisim project assign1.circ as structural Verilog: 5 circuits, main circuit main
module main (
  input  VolUp,
  input  VolDown
);

  wire and_1_out, and_2_out, and_3_out, and_4_out, and_5_out, and_6_out, and_7_out, and_8_out, and_9_out,
       and_10_out, and_11_out, and_12_out, and_13_out, and_14_out, and_15_out, and_16_out, and_17_out,
       clock_1_out, d_ff_1_q, d_ff_2_q, d_ff_3_q, d_ff_4_q, d_ff_5_q, d_ff_6_q, d_ff_7_q, d_ff_8_q, d_ff_9_q,
       d_ff_10_q, j_k_ff_1_q, j_k_ff_1_qn, not_1_out, or_1_out, or_2_out, or_3_out, or_4_out, or_5_out,
       or_6_out, or_7_out, or_8_out, or_9_out, or_10_out, Pause_out, Play_out;

  Clock clock_1 (.out(clock_1_out));
  Button Play (.out(Play_out));
  Button Pause (.out(Pause_out));
  or or_1 (or_1_out, VolDown, VolUp);
  D_Flip_Flop d_ff_1 (.D(Play_out), .clk(clock_1_out), .Q(d_ff_1_q), .preset(Play_out));  // open: Qn, reset
  D_Flip_Flop d_ff_2 (.D(Pause_out), .clk(clock_1_out), .Q(d_ff_2_q), .preset(Pause_out));  // open: Qn, reset
  not not_1 (not_1_out, VolUp);
  and and_1 (and_1_out, VolUp, VolUp);
  and and_2 (and_2_out, not_1_out, d_ff_4_q);
  or or_2 (or_2_out, and_1_out, and_2_out);
  D_Flip_Flop d_ff_3 (.D(or_2_out), .clk(and_3_out), .Q(d_ff_3_q));  // open: Qn, preset, reset
  and and_3 (and_3_out, or_1_out, clock_1_out);
  or or_3 (or_3_out, d_ff_1_q, d_ff_2_q);
  and and_4 (and_4_out, d_ff_3_q, VolUp);
  or or_4 (or_4_out, and_4_out, and_5_out);
  LED Vol0 (.in(d_ff_3_q));
  J_K_Flip_Flop j_k_ff_1 (
    .J(or_3_out), .K(d_ff_2_q), .clk(clock_1_out), .Q(j_k_ff_1_q), .Qn(j_k_ff_1_qn));  // open: preset, reset
  and and_5 (and_5_out, not_1_out, d_ff_5_q);
  D_Flip_Flop d_ff_4 (.D(or_4_out), .clk(and_3_out), .Q(d_ff_4_q));  // open: Qn, preset, reset
  LED Vol1 (.in(d_ff_4_q));
  LED Playing (.in(j_k_ff_1_q));
  LED Paused (.in(j_k_ff_1_qn));
  and and_6 (and_6_out, d_ff_4_q, VolUp);
  and and_7 (and_7_out, not_1_out, d_ff_6_q);
  or or_5 (or_5_out, and_6_out, and_7_out);
  D_Flip_Flop d_ff_5 (.D(or_5_out), .clk(and_3_out), .Q(d_ff_5_q));  // open: Qn, preset, reset
  and and_8 (and_8_out, d_ff_5_q, VolUp);
  and and_9 (and_9_out, not_1_out, d_ff_7_q);
  or or_6 (or_6_out, and_8_out, and_9_out);
  D_Flip_Flop d_ff_6 (.D(or_6_out), .clk(and_3_out), .Q(d_ff_6_q));  // open: Qn, preset, reset
  LED Vol2 (.in(d_ff_5_q));
  and and_10 (and_10_out, d_ff_6_q, VolUp);
  LED Vol3 (.in(d_ff_6_q));
  and and_11 (and_11_out, not_1_out, d_ff_8_q);
  or or_7 (or_7_out, and_10_out, and_11_out);
  D_Flip_Flop d_ff_7 (.D(or_7_out), .clk(and_3_out), .Q(d_ff_7_q));  // open: Qn, preset, reset
  LED Vol4 (.in(d_ff_7_q));
  and and_12 (and_12_out, d_ff_7_q, VolUp);
  and and_13 (and_13_out, not_1_out, d_ff_9_q);
  or or_8 (or_8_out, and_12_out, and_13_out);
  D_Flip_Flop d_ff_8 (.D(or_8_out), .clk(and_3_out), .Q(d_ff_8_q));  // open: Qn, preset, reset
  and and_14 (and_14_out, d_ff_8_q, VolUp);
  or or_9 (or_9_out, and_14_out, and_16_out);
  D_Flip_Flop d_ff_9 (.D(or_9_out), .clk(and_3_out), .Q(d_ff_9_q));  // open: Qn, preset, reset
  LED Vol5 (.in(d_ff_8_q));
  and and_15 (and_15_out, d_ff_9_q, VolUp);
  and and_16 (and_16_out, not_1_out, d_ff_10_q);
  LED Vol6 (.in(d_ff_9_q));
  and and_17 (and_17_out, not_1_out, 1'b0);
  or or_10 (or_10_out, and_15_out, and_17_out);
  D_Flip_Flop d_ff_10 (.D(or_10_out), .clk(and_3_out), .Q(d_ff_10_q));  // open: Qn, preset, reset
  LED Vol7 (.in(d_ff_10_q));
endmodule

module StageOne (
);

  wire clock_1_out, d_ff_1_q, d_ff_2_q, j_k_ff_1_q, j_k_ff_1_qn, or_1_out, Pause_out, Play_out;

  Clock clock_1 (.out(clock_1_out));
  Button Play (.out(Play_out));
  Button Pause (.out(Pause_out));
  D_Flip_Flop d_ff_1 (.D(Play_out), .clk(clock_1_out), .Q(d_ff_1_q), .preset(Play_out));  // open: Qn, reset
  D_Flip_Flop d_ff_2 (.D(Pause_out), .clk(clock_1_out), .Q(d_ff_2_q), .preset(Pause_out));  // open: Qn, reset
  or or_1 (or_1_out, d_ff_1_q, d_ff_2_q);
  J_K_Flip_Flop j_k_ff_1 (
    .J(or_1_out), .K(d_ff_2_q), .clk(clock_1_out), .Q(j_k_ff_1_q), .Qn(j_k_ff_1_qn));  // open: preset, reset
  LED Playing (.in(j_k_ff_1_q));
  LED Paused (.in(j_k_ff_1_qn));
endmodule

module StageTwo (
  input  VolUp,
  input  VolDown
);

  wire and_1_out, and_2_out, and_3_out, and_4_out, and_5_out, and_6_out, and_7_out, and_8_out, and_9_out,
       and_10_out, and_11_out, and_12_out, and_13_out, and_14_out, and_15_out, and_16_out, and_17_out,
       clock_1_out, d_ff_1_q, d_ff_2_q, d_ff_3_q, d_ff_4_q, d_ff_5_q, d_ff_6_q, d_ff_7_q, d_ff_8_q,
       not_1_out, or_1_out, or_2_out, or_3_out, or_4_out, or_5_out, or_6_out, or_7_out, or_8_out, or_9_out;

  or or_1 (or_1_out, VolDown, VolUp);
  Clock clock_1 (.out(clock_1_out));
  not not_1 (not_1_out, VolUp);
  and and_1 (and_1_out, not_1_out, d_ff_2_q);
  and and_2 (and_2_out, VolUp, VolUp);
  or or_2 (or_2_out, and_2_out, and_1_out);
  D_Flip_Flop d_ff_1 (.D(or_2_out), .clk(and_3_out), .Q(d_ff_1_q));  // open: Qn, preset, reset
  and and_3 (and_3_out, or_1_out, clock_1_out);
  and and_4 (and_4_out, d_ff_1_q, VolUp);
  or or_3 (or_3_out, and_4_out, and_5_out);
  LED Vol0 (.in(d_ff_1_q));
  and and_5 (and_5_out, not_1_out, d_ff_3_q);
  D_Flip_Flop d_ff_2 (.D(or_3_out), .clk(and_3_out), .Q(d_ff_2_q));  // open: Qn, preset, reset
  LED Vol1 (.in(d_ff_2_q));
  and and_6 (and_6_out, d_ff_2_q, VolUp);
  and and_7 (and_7_out, not_1_out, d_ff_4_q);
  or or_4 (or_4_out, and_6_out, and_7_out);
  D_Flip_Flop d_ff_3 (.D(or_4_out), .clk(and_3_out), .Q(d_ff_3_q));  // open: Qn, preset, reset
  and and_8 (and_8_out, d_ff_3_q, VolUp);
  and and_9 (and_9_out, not_1_out, d_ff_5_q);
  or or_5 (or_5_out, and_8_out, and_9_out);
  D_Flip_Flop d_ff_4 (.D(or_5_out), .clk(and_3_out), .Q(d_ff_4_q));  // open: Qn, preset, reset
  LED Vol2 (.in(d_ff_3_q));
  and and_10 (and_10_out, d_ff_4_q, VolUp);
  LED Vol3 (.in(d_ff_4_q));
  and and_11 (and_11_out, not_1_out, d_ff_6_q);
  or or_6 (or_6_out, and_10_out, and_11_out);
  D_Flip_Flop d_ff_5 (.D(or_6_out), .clk(and_3_out), .Q(d_ff_5_q));  // open: Qn, preset, reset
  LED Vol4 (.in(d_ff_5_q));
  and and_12 (and_12_out, not_1_out, d_ff_7_q);
  and and_13 (and_13_out, d_ff_5_q, VolUp);
  or or_7 (or_7_out, and_13_out, and_12_out);
  D_Flip_Flop d_ff_6 (.D(or_7_out), .clk(and_3_out), .Q(d_ff_6_q));  // open: Qn, preset, reset
  and and_14 (and_14_out, d_ff_6_q, VolUp);
  or or_8 (or_8_out, and_14_out, and_15_out);
  D_Flip_Flop d_ff_7 (.D(or_8_out), .clk(and_3_out), .Q(d_ff_7_q));  // open: Qn, preset, reset
  LED Vol5 (.in(d_ff_6_q));
  and and_15 (and_15_out, not_1_out, d_ff_8_q);
  and and_16 (and_16_out, d_ff_7_q, VolUp);
  LED Vol6 (.in(d_ff_7_q));
  and and_17 (and_17_out, not_1_out, 1'b0);
  or or_9 (or_9_out, and_16_out, and_17_out);
  D_Flip_Flop d_ff_8 (.D(or_9_out), .clk(and_3_out), .Q(d_ff_8_q));  // open: Qn, preset, reset
  LED Vol7 (.in(d_ff_8_q));
endmodule

module StageThree (
  input  in_1,
  input  in_2,
  input  in_3,
  input  in_4
);

  wire and_1_out, and_2_out, and_3_out, and_4_out, clock_1_out, clock_2_out, j_k_ff_1_q, j_k_ff_1_qn,
       j_k_ff_2_q, j_k_ff_4_q, j_k_ff_4_qn, not_1_out, or_1_out, or_2_out, xnor_1_out, xnor_2_out;

  Clock clock_1 (.out(clock_1_out));
  xnor xnor_1 (xnor_1_out, in_2, clock_1_out);
  J_K_Flip_Flop j_k_ff_1 (
    .J(in_3), .K(in_3), .clk(clock_2_out), .Q(j_k_ff_1_q), .Qn(j_k_ff_1_qn));  // open: preset, reset
  Clock clock_2 (.out(clock_2_out));
  J_K_Flip_Flop j_k_ff_2 (.J(in_1), .K(in_1), .clk(xnor_1_out), .Q(j_k_ff_2_q));  // open: Qn, preset, reset
  not not_1 (not_1_out, in_4);
  xnor xnor_2 (xnor_2_out, j_k_ff_2_q, in_2);
  and and_1 (and_1_out, in_4, j_k_ff_1_q);
  or or_1 (or_1_out, and_1_out, and_2_out);
  and and_2 (and_2_out, j_k_ff_1_qn, not_1_out);
  J_K_Flip_Flop j_k_ff_3 (.J(in_1), .K(in_1), .clk(xnor_2_out));  // open: Q, Qn, preset, reset
  J_K_Flip_Flop j_k_ff_4 (
    .J(or_1_out), .K(or_1_out), .clk(clock_2_out), .Q(j_k_ff_4_q), .Qn(j_k_ff_4_qn));  // open: preset, reset
  and and_3 (and_3_out, and_1_out, j_k_ff_4_q);
  and and_4 (and_4_out, j_k_ff_4_qn, and_2_out);
  J_K_Flip_Flop j_k_ff_5 (.J(or_2_out), .K(or_2_out), .clk(clock_2_out));  // open: Q, Qn, preset, reset
  or or_2 (or_2_out, and_3_out, and_4_out);
endmodule

module ButtonStateHolder (
);

  wire button_1_out, clock_1_out, d_ff_1_q;

  Button button_1 (.out(button_1_out));
  Clock clock_1 (.out(clock_1_out));
  D_Flip_Flop d_ff_1 (.D(button_1_out), .clk(clock_1_out), .Q(d_ff_1_q), .preset(button_1_out));  // open: Qn, reset
  D_Flip_Flop d_ff_2 (.D(d_ff_1_q), .clk(clock_1_out));  // open: Q, Qn, preset, reset
endmodule
